// Logisim project FullAdder.circ as structural Verilog
module FullAdder (
  input  X,
  input  Y,
  input  Cin,
  output Sum,
  output Cout
);

  wire and_1_out, and_2_out, or_1_out, xor_1_out, xor_2_out;

  xor xor_1 (xor_1_out, X, Y);
  and and_1 (and_1_out, Cin, xor_1_out);
  and and_2 (and_2_out, X, Y);
  xor xor_2 (xor_2_out, xor_1_out, Cin);
  or or_1 (or_1_out, and_1_out, and_2_out);
endmodule
