// Logisim project Module 12.circ as structural Verilog
module FullAdder (
  input  X,
  input  Y,
  input  Cin,
  output Sum,
  output Cout
);

  wire and_1_out, and_2_out, xor_1_out;

  xor xor_1 (xor_1_out, X, Y);
  and and_1 (and_1_out, Cin, xor_1_out);
  and and_2 (and_2_out, X, Y);
  xor xor_2 (Sum, xor_1_out, Cin);
  or or_1 (Cout, and_1_out, and_2_out);
endmodule

module _8BitAdder (
  input  [7:0] Operand_A,
  input  [7:0] Operand_B,
  output Final_Carry,
  output [7:0] Final_sum
);

  wire fulladder_1_cout, fulladder_2_cout, fulladder_3_cout, fulladder_4_cout, fulladder_5_cout,
       fulladder_6_cout, fulladder_7_cout;

  FullAdder fulladder_1 (.X(Operand_A[0]), .Y(Operand_B[0]), .Sum(Final_sum[0]), .Cin(1'b0), .Cout(fulladder_1_cout));
  FullAdder fulladder_2 (
    .X(Operand_A[2]), .Y(Operand_B[2]), .Sum(Final_sum[2]), .Cin(fulladder_3_cout), .Cout(fulladder_2_cout));
  FullAdder fulladder_3 (
    .X(Operand_A[1]), .Y(Operand_B[1]), .Sum(Final_sum[1]), .Cin(fulladder_1_cout), .Cout(fulladder_3_cout));
  FullAdder fulladder_4 (
    .X(Operand_A[3]), .Y(Operand_B[3]), .Sum(Final_sum[3]), .Cin(fulladder_2_cout), .Cout(fulladder_4_cout));
  FullAdder fulladder_5 (
    .X(Operand_A[4]), .Y(Operand_B[4]), .Sum(Final_sum[4]), .Cin(fulladder_4_cout), .Cout(fulladder_5_cout));
  FullAdder fulladder_6 (
    .X(Operand_A[5]), .Y(Operand_B[5]), .Sum(Final_sum[5]), .Cin(fulladder_5_cout), .Cout(fulladder_6_cout));
  FullAdder fulladder_7 (
    .X(Operand_A[6]), .Y(Operand_B[6]), .Sum(Final_sum[6]), .Cin(fulladder_6_cout), .Cout(fulladder_7_cout));
  FullAdder fulladder_8 (
    .X(Operand_A[7]), .Y(Operand_B[7]), .Sum(Final_sum[7]), .Cin(fulladder_7_cout), .Cout(Final_Carry));
endmodule

module Decoder1Bit (
  input  A,
  input  B,
  input  Cin,
  output Sum,
  output Cout
);

  wire decoder_1_out1, decoder_1_out2, decoder_1_out3, decoder_1_out4, decoder_1_out5, decoder_1_out6,
       decoder_1_out7;

  Decoder #(.select(3), .enable("false")) decoder_1 (
    .out1(decoder_1_out1), .out2(decoder_1_out2), .out3(decoder_1_out3), .out4(decoder_1_out4),
    .out5(decoder_1_out5), .out6(decoder_1_out6), .out7(decoder_1_out7), .sel({A, B, Cin}));  // open: out0
  or or_1 (Sum, decoder_1_out1, decoder_1_out2, decoder_1_out4, decoder_1_out7);
  or or_2 (Cout, decoder_1_out3, decoder_1_out5, decoder_1_out6, decoder_1_out7);
endmodule

module Decoder4Bit (
  input  [3:0] Operand_A,
  input  [3:0] Operand_B,
  output [3:0] out_3,
  output Final_Carry
);

  wire decoder1bit_1_cout, decoder1bit_2_cout, decoder1bit_3_cout;

  Decoder1Bit decoder1bit_1 (.A(Operand_A[0]), .B(Operand_B[0]), .Cin(1'b0), .Sum(out_3[0]), .Cout(decoder1bit_1_cout));
  Decoder1Bit decoder1bit_2 (
    .A(Operand_A[1]), .B(Operand_B[1]), .Cin(decoder1bit_1_cout), .Sum(out_3[1]), .Cout(decoder1bit_2_cout));
  Decoder1Bit decoder1bit_3 (
    .A(Operand_A[2]), .B(Operand_B[2]), .Cin(decoder1bit_2_cout), .Sum(out_3[2]), .Cout(decoder1bit_3_cout));
  Decoder1Bit decoder1bit_4 (
    .A(Operand_A[3]), .B(Operand_B[3]), .Cin(decoder1bit_3_cout), .Sum(out_3[3]), .Cout(Final_Carry));
endmodule

module _8BitMux (
  input  [1:0] Selector,
  output [7:0] Mux_out
);

  Multiplexer #(.select(2), .width(8), .enable("false")) multiplexer_1 (
    .in0(8'h8), .in1(8'h10), .in2(8'h20), .in3(8'h40), .out(Mux_out), .sel(Selector));
endmodule

module _16to1Mux (
  input  [3:0] Selector,
  output [7:0] out_2
);

  wire [7:0] multiplexer_1_out, multiplexer_2_out, multiplexer_3_out, multiplexer_4_out;

  Multiplexer #(.select(2), .width(8), .enable("false")) multiplexer_1 (
    .in0(8'h1), .in1(8'h2), .in2(8'h3), .in3(8'h4), .out(multiplexer_1_out), .sel(Selector[1:0]));
  Multiplexer #(.select(2), .width(8), .enable("false")) multiplexer_2 (
    .in0(8'h5), .in1(8'h6), .in2(8'h7), .in3(8'h8), .out(multiplexer_2_out), .sel(Selector[1:0]));
  Multiplexer #(.select(2), .width(8), .enable("false")) multiplexer_3 (
    .in0(8'h9), .in1(8'h10), .in2(8'h11), .in3(8'h12), .out(multiplexer_3_out), .sel(Selector[1:0]));
  Multiplexer #(.select(2), .width(8), .enable("false")) multiplexer_4 (
    .in0(8'h13), .in1(8'h14), .in2(8'h15), .in3(8'h16), .out(multiplexer_4_out), .sel(Selector[1:0]));
  Multiplexer #(.select(2), .width(8), .enable("false")) multiplexer_5 (
    .in0(multiplexer_1_out), .in1(multiplexer_2_out), .in2(multiplexer_3_out), .in3(multiplexer_4_out),
    .out(out_2), .sel(Selector[3:2]));
endmodule
