// Logisim project problem1.circ as structural Verilog: 1 circuit, main circuit main
module main (
  output out_1,
  output out_2
);

  wire clock_1_out, not_1_out, Q0_q, Q1_q, xor_1_out;

  D_Flip_Flop Q0 (.clk(clock_1_out), .D(not_1_out), .Q(Q0_q), .Qn(out_1));  // open: preset, en, reset
  Clock clock_1 (.out(clock_1_out));
  D_Flip_Flop Q1 (.clk(clock_1_out), .D(xor_1_out), .Q(Q1_q), .Qn(out_2));  // open: preset, en, reset
  not not_1 (not_1_out, Q0_q);
  xor xor_1 (xor_1_out, Q0_q, Q1_q);
endmodule
