// Logisim project problem2.circ as structural Verilog: 1 circuit, main circuit Problem2
module Problem2 (
  output out_1,
  output out_2,
  output out_3
);

  wire clock_1_out;
  wire [2:0] Q2_q, rom_1_data;

  Clock clock_1 (.out(clock_1_out));
  D_Flip_Flop Q2 (.clk(clock_1_out), .D(rom_1_data[0]), .Q(Q2_q[0]), .Qn(out_1));  // open: preset, en, reset
  D_Flip_Flop Q1 (.clk(clock_1_out), .D(rom_1_data[1]), .Q(Q2_q[1]), .Qn(out_2));  // open: preset, en, reset
  D_Flip_Flop Q0 (.clk(clock_1_out), .D(rom_1_data[2]), .Q(Q2_q[2]), .Qn(out_3));  // open: preset, en, reset
  ROM #(.addrWidth(3), .dataWidth(3)) rom_1 (.addr(Q2_q), .data(rom_1_data));  // open: sel

  // Notes on the sheet:
  //   contents of rom_1 (hex, n*v repeats v):
  //   1 2 3 4 5
endmodule
